// Logisim project FPA.circ as structural Verilog: 2 circuits, main circuit main
module main (
  input  [31:0] A,
  input  [31:0] B,
  output [31:0] Result,
  output out_4,
  output out_5
);

  FPA fpa_1 (.A(A), .B(B), .Result(Result), .out_4(out_4), .out_5(out_5));
endmodule

module FPA (
  input  [31:0] A,
  input  [31:0] B,
  output [31:0] Result,
  output out_4,
  output out_5
);

  wire addedinp_1_p3, addedinp_1_p4, addedinp_1_p5, addedinp_1_p6, addedinp_1_p7, addedinp_1_p8,
       addedinp_1_p9, addedinp_1_p10, addedinp_1_p11, inputcheck_1_p3, n0handler_1_p2, n0handler_2_p2,
       n11adder_1_p4, n32mux4x1_1_p4, n32to20_1_p2, n7408_1_p3, normalization_1_p7, normalization_1_p8,
       normalization_1_p9, outputprocess_1_p4, roundingmachine_1_p2, roundingmachine_1_p3;

  // _0handler 0handler_1: pin names not known; wires that end beside it: A, n0handler_1_p2
  // _0handler 0handler_2: pin names not known; wires that end beside it: B, n0handler_2_p2
  // InputCheck inputcheck_1: pin names not known; wires that end beside it: n0handler_1_p2, n0handler_2_p2, inputcheck_1_p3
  // AddedInp addedinp_1: pin names not known; wires that end beside it: n0handler_1_p2, n0handler_2_p2, addedinp_1_p3, addedinp_1_p4, addedinp_1_p5, addedinp_1_p6, addedinp_1_p7, addedinp_1_p8, addedinp_1_p9, addedinp_1_p10, addedinp_1_p11
  // Normalization normalization_1: pin names not known; wires that end beside it: addedinp_1_p5, addedinp_1_p6, addedinp_1_p7, addedinp_1_p10, addedinp_1_p11, addedinp_1_p8, normalization_1_p7, normalization_1_p8, normalization_1_p9
  // RoundingMachine roundingmachine_1: pin names not known; wires that end beside it: normalization_1_p8, roundingmachine_1_p2, roundingmachine_1_p3
  // _11Adder 11adder_1: pin names not known; wires that end beside it: addedinp_1_p10, normalization_1_p9, roundingmachine_1_p3, n11adder_1_p4
  // _32to20 32to20_1: pin names not known; wires that end beside it: roundingmachine_1_p2, n32to20_1_p2
  // OutputProcess outputprocess_1: pin names not known; wires that end beside it: addedinp_1_p9, n11adder_1_p4, n32to20_1_p2, outputprocess_1_p4
  // OverflowTest_main main_1: pin names not known; wires that end beside it: addedinp_1_p10, normalization_1_p9, 11'h1, 1'b0, 1'b0, out_4
  // Underflow_main main_2: pin names not known; wires that end beside it: addedinp_1_p10, normalization_1_p9, out_5
  // _7408 7408_1: pin names not known; wires that end beside it: inputcheck_1_p3, addedinp_1_p4, n7408_1_p3, 1'b1
  // _32Mux4X1 32mux4x1_1: pin names not known; wires that end beside it: 1'b0, n0handler_2_p2, n0handler_1_p2, n32mux4x1_1_p4, n32mux4x1_1_p4, n7408_1_p3, addedinp_1_p3, 1'b0, Result
  // _32Mux2X1 32mux2x1_1: pin names not known; wires that end beside it: {32{1'b0}}, outputprocess_1_p4, 1'b0, normalization_1_p7, n32mux4x1_1_p4
endmodule
