// Logisim project InputHandler.circ as structural Verilog: 2 circuits, main circuit ExpDiff12
// ExpDiff
module ExpDiff12 (
  input  SA,
  input  SB,
  input  [10:0] A,
  input  [10:0] B,
  output Switch,
  output A_B,
  output [10:0] A_nB,
  output [10:0] Exp_Large
);

  wire n11mux2x1_1_p5;

  // _11BitMagnitudeComparator 11bitmagnitudecomparator_1: pin names not known; wires that end beside it: SA, SB, A, B, Switch, A_B
  // _11Mux2X1 11mux2x1_1: pin names not known; wires that end beside it: A, B, 1'b0, A_B, n11mux2x1_1_p5
  // _11Mux2X1 11mux2x1_2: pin names not known; wires that end beside it: B, A, 1'b0, A_B, Exp_Large
  // _11Sub 11sub_1: pin names not known; wires that end beside it: Exp_Large, n11mux2x1_1_p5, A_nB
endmodule

// InpProc
module InputHandle (
  input  SA,
  input  SB,
  input  [31:0] Fraction1,
  input  [31:0] Fraction2,
  input  [10:0] A_Exp,
  input  [10:0] B_Exp,
  output Switch,
  output [31:0] Large,
  output [31:0] Small,
  output [10:0] ExpDiff,
  output [10:0] Exp_Large,
  output A_B
);

  ExpDiff12 expdiff12_1 (
    .SA(SA), .SB(SB), .A(A_Exp), .B(B_Exp), .Switch(Switch), .A_B(A_B), .A_nB(ExpDiff), .Exp_Large(Exp_Large));
  // _32Mux2X1 32mux2x1_1: pin names not known; wires that end beside it: Fraction2, Fraction1, 1'b0, A_B, Large
  // _32Mux2X1 32mux2x1_2: pin names not known; wires that end beside it: Fraction1, Fraction2, 1'b0, A_B, Small
endmodule
